// Logisim project Sim1.circ as structural Verilog: 1 circuit, main circuit main
module main (
  input  W,
  input  X,
  input  Y,
  input  Z,
  output out_5,
  output out_6,
  output out_7,
  output out_8
);

  wire and_1_out, and_2_out, and_3_out, and_4_out, and_5_out, and_6_out, and_7_out, not_1_out, not_2_out,
       not_3_out, not_4_out, not_5_out;

  not not_1 (not_1_out, X);
  not not_2 (not_2_out, Y);
  not not_3 (not_3_out, Z);
  not not_4 (not_4_out, Y);
  not not_5 (not_5_out, Z);
  not not_6 (out_8, Z);
  and and_1 (and_1_out, X, Y);
  and and_2 (and_2_out, X, Z);
  and and_3 (and_3_out, not_1_out, Y);
  and and_4 (and_4_out, not_1_out, Z);
  and and_5 (and_5_out, X, not_2_out, not_3_out);
  and and_6 (and_6_out, Y, Z);
  and and_7 (and_7_out, not_4_out, not_5_out);
  or or_1 (out_5, W, and_1_out, and_2_out);
  or or_2 (out_6, and_3_out, and_4_out, and_5_out);
  or or_3 (out_7, and_6_out, and_7_out);
endmodule
