// Logisim project AdderSubtractor.circ as structural Verilog: 2 circuits, main circuit main
module main (
  input  M,
  input  [3:0] A3_A2_A1_A0,
  input  [3:0] B3_B2_B1_B0,
  output out_4,
  output out_5,
  output out_6,
  output out_7,
  output C_out
);

  wire fulladder_1_acin_bcin_ab, fulladder_2_acin_bcin_ab, fulladder_3_acin_bcin_ab, xor_1_out, xor_2_out,
       xor_3_out, xor_4_out;

  xor xor_1 (xor_1_out, B3_B2_B1_B0[0], M);
  xor xor_2 (xor_2_out, B3_B2_B1_B0[1], M);
  xor xor_3 (xor_3_out, B3_B2_B1_B0[2], M);
  xor xor_4 (xor_4_out, B3_B2_B1_B0[3], M);
  FullAdder fulladder_1 (
    .A(A3_A2_A1_A0[0]), .B(xor_1_out), .Cin(M), .out_4(out_4), .ACin_BCin_AB(fulladder_1_acin_bcin_ab));
  FullAdder fulladder_2 (
    .A(A3_A2_A1_A0[1]), .B(xor_2_out), .Cin(fulladder_1_acin_bcin_ab), .out_4(out_5),
    .ACin_BCin_AB(fulladder_2_acin_bcin_ab));
  FullAdder fulladder_3 (
    .A(A3_A2_A1_A0[2]), .B(xor_3_out), .Cin(fulladder_2_acin_bcin_ab), .out_4(out_6),
    .ACin_BCin_AB(fulladder_3_acin_bcin_ab));
  FullAdder fulladder_4 (
    .A(A3_A2_A1_A0[3]), .B(xor_4_out), .Cin(fulladder_3_acin_bcin_ab), .out_4(out_7), .ACin_BCin_AB(C_out));

  // Notes on the sheet:
  //   C in
  //   C in
  //   C in
  //   C in
endmodule

module FullAdder (
  input  A,
  input  B,
  input  Cin,
  output out_4,
  output ACin_BCin_AB
);

  wire and_1_out, and_2_out, and_3_out, xor_1_out;

  xor xor_1 (xor_1_out, A, B);
  xor xor_2 (out_4, xor_1_out, Cin);
  and and_1 (and_1_out, A, Cin);
  and and_2 (and_2_out, B, Cin);
  and and_3 (and_3_out, A, B);
  or or_1 (ACin_BCin_AB, and_1_out, and_2_out, and_3_out);

  // Notes on the sheet:
  //   A'B+AB'
  //   ACin
  //   BCin
  //   AB
  //   (A'B'+AB)Cin+Cin'(A'B+AB')
endmodule
