// Logisim project BCD_adder.circ as structural Verilog: 2 circuits, main circuit main
module main (
  input  in_1,
  input  in_2,
  input  [3:0] in_3,
  input  [3:0] in_4,
  input  in_5,
  output S1,
  output S2,
  output S3,
  output S4,
  output Carry
);

  wire and_1_out, and_2_out, full_adder_1_acin_bcin_ab, full_adder_1_out_4, full_adder_2_acin_bcin_ab,
       full_adder_2_out_4, full_adder_3_acin_bcin_ab, full_adder_3_out_4, full_adder_4_acin_bcin_ab,
       full_adder_4_out_4, full_adder_5_acin_bcin_ab, full_adder_6_acin_bcin_ab, full_adder_7_acin_bcin_ab,
       or_1_out, or_2_out;

  Full_Adder full_adder_1 (
    .A(in_3[0]), .out_4(full_adder_1_out_4), .B(in_4[0]), .Cin(in_1), .ACin_BCin_AB(full_adder_1_acin_bcin_ab));
  Full_Adder full_adder_2 (
    .A(in_3[1]), .out_4(full_adder_2_out_4), .B(in_4[1]), .Cin(full_adder_1_acin_bcin_ab),
    .ACin_BCin_AB(full_adder_2_acin_bcin_ab));
  Full_Adder full_adder_3 (
    .A(in_3[2]), .out_4(full_adder_3_out_4), .B(in_4[2]), .Cin(full_adder_2_acin_bcin_ab),
    .ACin_BCin_AB(full_adder_3_acin_bcin_ab));
  Full_Adder full_adder_4 (
    .A(in_3[3]), .out_4(full_adder_4_out_4), .B(in_4[3]), .Cin(full_adder_3_acin_bcin_ab),
    .ACin_BCin_AB(full_adder_4_acin_bcin_ab));
  and and_1 (and_1_out, full_adder_3_out_4, full_adder_4_out_4);
  and and_2 (and_2_out, full_adder_4_out_4, full_adder_2_out_4);
  or or_1 (or_1_out, and_1_out, and_2_out);
  or or_2 (or_2_out, or_1_out, full_adder_4_acin_bcin_ab);
  Full_Adder full_adder_5 (
    .A(full_adder_1_out_4), .out_4(S1), .B(in_5), .Cin(in_2), .ACin_BCin_AB(full_adder_5_acin_bcin_ab));
  Full_Adder full_adder_6 (
    .A(full_adder_2_out_4), .out_4(S2), .B(or_2_out), .Cin(full_adder_5_acin_bcin_ab),
    .ACin_BCin_AB(full_adder_6_acin_bcin_ab));
  Full_Adder full_adder_7 (
    .A(full_adder_3_out_4), .out_4(S3), .B(or_2_out), .Cin(full_adder_6_acin_bcin_ab),
    .ACin_BCin_AB(full_adder_7_acin_bcin_ab));
  Full_Adder full_adder_8 (
    .A(full_adder_4_out_4), .out_4(S4), .B(in_5), .Cin(full_adder_7_acin_bcin_ab), .ACin_BCin_AB(Carry));

  // Notes on the sheet:
  //   K
endmodule

module Full_Adder (
  input  A,
  input  B,
  input  Cin,
  output out_4,
  output ACin_BCin_AB
);

  wire and_1_out, and_2_out, and_3_out, xor_1_out;

  xor xor_1 (xor_1_out, A, B);
  xor xor_2 (out_4, xor_1_out, Cin);
  and and_1 (and_1_out, A, Cin);
  and and_2 (and_2_out, B, Cin);
  and and_3 (and_3_out, A, B);
  or or_1 (ACin_BCin_AB, and_1_out, and_2_out, and_3_out);

  // Notes on the sheet:
  //   A'B+AB'
  //   ACin
  //   BCin
  //   AB
  //   (A'B'+AB)Cin+Cin'(A'B+AB')
endmodule
