// Logisim project FullAdder.circ as structural Verilog: 1 circuit, main circuit main
module main (
  input  A,
  input  B,
  input  Cin,
  output out_4,
  output ACin_BCin_AB
);

  wire and_1_out, and_2_out, and_3_out, xor_1_out;

  xor xor_1 (xor_1_out, A, B);
  xor xor_2 (out_4, xor_1_out, Cin);
  and and_1 (and_1_out, A, Cin);
  and and_2 (and_2_out, B, Cin);
  and and_3 (and_3_out, A, B);
  or or_1 (ACin_BCin_AB, and_1_out, and_2_out, and_3_out);

  // Notes on the sheet:
  //   A'B+AB'
  //   ACin
  //   BCin
  //   AB
  //   (A'B'+AB)Cin+Cin'(A'B+AB')
endmodule
