// Logisim project 8to1MUX.circ as structural Verilog: 2 circuits, main circuit main
// 8:1MUX
module main (
  input  I0,
  input  I1,
  input  I2,
  input  I3,
  input  I4,
  input  I5,
  input  I6,
  input  I7,
  input  S1,
  input  E,
  input  S0,
  input  S2,
  output Y_prime,
  output Y
);

  wire and_1_out, and_2_out, and_3_out, and_4_out, and_5_out, and_6_out, and_7_out, and_8_out, not_1_out,
       not_2_out, not_3_out, not_4_out;

  not not_1 (not_1_out, S2);
  not not_2 (not_2_out, S0);
  not not_3 (not_3_out, S1);
  not not_4 (not_4_out, E);
  and and_1 (and_1_out, I0, not_2_out, not_3_out, not_1_out, not_4_out);
  and and_2 (and_2_out, I1, S0, not_3_out, not_1_out, not_4_out);
  and and_3 (and_3_out, I2, not_2_out, S1, not_1_out, not_4_out);
  and and_4 (and_4_out, I3, S0, S1, not_1_out, not_4_out);
  and and_5 (and_5_out, I4, not_2_out, not_3_out, S2, not_4_out);
  and and_6 (and_6_out, I5, S0, not_3_out, S2, not_4_out);
  and and_7 (and_7_out, I6, not_2_out, S1, S2, not_4_out);
  and and_8 (and_8_out, I7, S0, S1, S2, not_4_out);
  or or_1 (Y, and_1_out, and_2_out, and_3_out, and_4_out, and_5_out, and_6_out, and_7_out, and_8_out);
  not not_5 (Y_prime, Y);
endmodule

module ImplementIC (
  input  in_1,
  input  A,
  input  in_3,
  input  S0,
  input  S1,
  input  S2,
  input  E,
  output Y,
  output Y_2
);

  wire not_1_out;

  not not_1 (not_1_out, A);
  main main_1 (
    .I0(in_1), .I1(in_1), .I2(in_3), .I3(not_1_out), .I4(in_3), .I5(not_1_out), .I6(A), .I7(A), .Y_prime(Y),
    .Y(Y_2), .S0(S0), .S1(S1), .S2(S2), .E(E));
endmodule
