// Logisim project AllSimulations.circ as structural Verilog: 1 circuit, main circuit main
module main (
  input  J,
  input  K,
  input  T,
  input  in_4,
  input  D,
  input  Preset,
  input  Clear,
  output Q,
  output Q_prime,
  output out_10,
  output out_11,
  output out_12,
  output out_13,
  output out_14
);

  wire and_1_out, and_2_out, and_3_out, and_4_out, Clk_2_out, Clk_3_out, Clk_4_out, Clk_out, d_ff_1_q,
       d_ff_2_q, d_ff_3_q, nand_1_out, nand_2_out, not_1_out;

  Clock Clk (.out(Clk_out));
  Clock Clk_2 (.out(Clk_2_out));
  Clock Clk_3 (.out(Clk_3_out));
  not not_1 (not_1_out, in_4);
  D_Flip_Flop d_ff_1 (.D(D), .Q(d_ff_1_q), .preset(Preset), .en(Clk_4_out), .reset(Clear));  // open: clk, Qn
  Clock Clk_4 (.out(Clk_4_out));
  and and_1 (and_1_out, Q, J, Clk_out);
  and and_2 (and_2_out, Clk_out, K, Q_prime);
  and and_3 (and_3_out, out_10, T, Clk_2_out);
  and and_4 (and_4_out, Clk_2_out, T, out_11);
  D_Flip_Flop d_ff_2 (.D(d_ff_1_q), .Q(d_ff_2_q), .preset(Preset), .en(Clk_4_out), .reset(Clear));  // open: clk, Qn
  nand nand_1 (nand_1_out, in_4, Clk_3_out);
  nand nand_2 (nand_2_out, Clk_3_out, not_1_out);
  D_Flip_Flop d_ff_3 (.D(d_ff_2_q), .Q(d_ff_3_q), .preset(Preset), .en(Clk_4_out), .reset(Clear));  // open: clk, Qn
  nor nor_1 (Q, and_1_out, Q_prime);
  nor nor_2 (Q_prime, Q, and_2_out);
  nor nor_3 (out_10, and_3_out, out_11);
  nor nor_4 (out_11, out_10, and_4_out);
  nand nand_3 (out_12, nand_1_out, out_13);
  nand nand_4 (out_13, out_12, nand_2_out);
  D_Flip_Flop d_ff_4 (.D(d_ff_3_q), .Q(out_14), .preset(Preset), .en(Clk_4_out), .reset(Clear));  // open: clk, Qn
endmodule
