// Logisim project SeqCkt.circ as structural Verilog: 2 circuits, main circuit main
module main (
  input  Clear,
  input  Preset,
  input  X,
  output out_4
);

  wire and_2_out, Clk_out, d_ff_1_q, not_1_out, not_2_out, xor_1_out;

  Clock Clk (.out(Clk_out));
  not not_1 (not_1_out, d_ff_1_q);
  not not_2 (not_2_out, X);
  and and_1 (out_4, X, not_1_out);
  xor xor_1 (xor_1_out, X, d_ff_1_q);
  and and_2 (and_2_out, not_2_out, not_1_out);
  D_Flip_Flop d_ff_1 (.D(xor_1_out), .Q(d_ff_1_q), .preset(Preset), .en(Clk_out), .reset(Clear));  // open: clk, Qn
  D_Flip_Flop d_ff_2 (.D(and_2_out), .preset(Preset), .en(Clk_out), .reset(Clear));  // open: clk, Q, Qn
endmodule

module SubCkt (
  input  in_1,
  input  in_2,
  output out_3,
  output out_4,
  output out_5
);

  wire not_1_out, not_2_out;

  not not_1 (not_1_out, in_2);
  not not_2 (not_2_out, in_1);
  and and_1 (out_3, in_1, not_1_out);
  xor xor_1 (out_4, in_1, in_2);
  and and_2 (out_5, not_2_out, not_1_out);
endmodule
